# Fritzing sketch DemoFritz 1.0 (saved by Fritzing 0.9.2b)
breadboards: 1

parts:
  Part1 = Arduino Mega 2560 (Rev3)
  U1 = XBee  # not connected
  U2 = XBee  # not connected
  LED2 = LED - 5mm [color="Yellow (595nm)" package="5 mm [THT]"]
  LED3 = LED - 5mm [color="Green (555nm)" package="5 mm [THT]"]

nets:
  N1: Part1.GND, LED2.cathode, LED3.anode

// code stored in the sketch: DemoFritz 1.0.ino
#include <Servo.h>

/*
  Blink
  Turns on an LED on for one second, then off for one second, repeatedly.

  Most Arduinos have an on-board LED you can control. On the Uno and
  Leonardo, it is attached to digital pin 13. If you're unsure what
  pin the on-board LED is connected to on your Arduino model, check
  the documentation at http://www.arduino.cc

  This example code is in the public domain.

  modified 8 May 2014
  by Scott Fitzgerald
 */

Servo myservo;
// the setup function runs once when you press reset or power the board
void setup() {
  // initialize digital pin 13 as an output.
  pinMode(10, OUTPUT);
  pinMode(11, OUTPUT);
  pinMode(12, OUTPUT);
  myservo.attach(9);
}

// the loop function runs over and over again forever
void loop() {
  digitalWrite(10, HIGH);   // turn the LED on (HIGH is the voltage level)
   myservo.write(90);
  delay(8000);              // wait for a second
 
  digitalWrite(10, LOW);    // turn the LED off by making the voltage LOW
  
  delay(1000);              // wait for a second
  
  digitalWrite(11, HIGH);   // turn the LED on (HIGH is the voltage level)
  delay(2000);              // wait for a second
  digitalWrite(11, LOW);    // turn the LED off by making the voltage LOW
  myservo.write(0);
  delay(1000);
  digitalWrite(12, HIGH);   // turn the LED on (HIGH is the voltage level)
  delay(12000);              // wait for a second
  digitalWrite(12, LOW);    // turn the LED off by making the voltage LOW
  delay(100);
}
