# Fritzing sketch Untitled Sketch (saved by Fritzing 0.9.2b)
breadboards: 1

parts:
  LED1 = LED - 5mm [color="Red (633nm)" package="5 mm [THT]"]
  Part1 = Arduino Mega ADK (Rev3)
  Part1_2 = Arduino Mega ADK (Rev3)

nets:
  N1: LED1.cathode, Part1_2.GND
  N2: LED1.anode, Part1.D13_PWM, Part1_2.D13_PWM
